# Fritzing sketch rpi-pico-relay (saved by Fritzing 1.0.0rc)
circuit board: 10.0043cm x 4.77016cm
breadboards: 1

parts:
  RasperryPi_Pico = Raspberry Pi Pico
  relay = QIANJI relay [part_number=JQC-3F]
  maintenance-rocker-switch = SWITCH-SPST-2 [package=switch-spst-vertical]
  output-usb-device = USB Connectors [package=usb-a-s-nosilk-female]
  input-usb-device = Adafruit USB Type C Breakout [part_number=4090]
  input-rpi-pico = Adafruit USB Type C Breakout [part_number=4090]
  D1 = Diode [package=diode-1n4001]
  R1 = Resistor [tolerance=±5% power=0.25W resistance=220 package=THT]
  Q1 = npn-Powertransistor [package="TO220 [THT]"]

nets:
  N1: RasperryPi_Pico.pin_1, R1.Pin_1
  N2: RasperryPi_Pico.pin_2, maintenance-rocker-switch.P
  N3: RasperryPi_Pico.pin_3, RasperryPi_Pico.pin_8, RasperryPi_Pico.pin_13, RasperryPi_Pico.pin_18, RasperryPi_Pico.pin_23, RasperryPi_Pico.pin_28, RasperryPi_Pico.pin_33, RasperryPi_Pico.pin_38, RasperryPi_Pico.pin_42, relay.DC1, input-rpi-pico.GND
  N4: RasperryPi_Pico.pin_40, maintenance-rocker-switch.O, input-rpi-pico.VBUS, Q1.collector
  N5: relay.NO, output-usb-device.VBUS
  N6: relay.COMMON, input-usb-device.VBUS
  N7: relay.DC2, D1.A
  GND: output-usb-device.GND, input-usb-device.GND
  N8: D1.C, Q1.emitter
  N9: R1.Pin_0, Q1.base

custom parts:
  Raspberry Pi Pico: Raspberry Pi Pico. Based around the RP2040 microcontroller the Pico is a low cost microcontroller device bringing Raspberry Pi quality, cost, and easy of use to the microcontroller space. Jan 2021, Split part in to two versions: tht (this one) and SMD. This one will drill holes for a .1 in header in pcb to allow plugging in the module as well as providing pads to solder the module to the top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
  QIANJI relay: QIANJI JQC-3F, adjusted pins
  Adafruit USB Type C Breakout: Adafruit breakout board for USB Type C socket.

// code stored in the sketch: Untitled.bas

